# Fritzing sketch LDL (saved by Fritzing 0.9.3b)
breadboards: 1

parts:
  SERVO1 = Tower Pro SG90 servo [part_number=101246]
  Part1 = Arduino Uno (Rev3)
  Part2 = Thumb Joystick
  LED1 = LED - 5mm [color="Red (633nm)" package="5 mm [THT]"]
  SERVO2 = Tower Pro SG90 servo [part_number=101246]

nets:
  N1: SERVO1.Signal, Part1.D3_PWM
  +5V: SERVO1.+5V, Part1.5V, Part2.VCC, SERVO2.+5V
  N2: Part1.A1, Part2.VERT
  N3: Part1.D10_PWM/SS, SERVO2.Signal
  N4: Part1.D13/SCK, LED1.anode
  GND: Part1.GND, Part2.GND, LED1.cathode
  N5: Part1.D2, Part2.SEL

custom parts:
  Tower Pro SG90 servo: Original file by John De Cristofaro http://www.adafruit.com/products/1449 Adafruit Feedback Servo (Small) Edited by: e-radionica.com 28/9/2015

// code stored in the sketch: LDL.ino
#include <Servo.h>


const int servo1 = 3;       
const int servo2 = 10;   
const int joyH = A1;       
const int joyV = A0;      


int servoVal;          
int button=0;
Servo myservo1;  
Servo myservo2;  


void setup() {
  pinMode(13, OUTPUT);
  pinMode(2, INPUT_PULLUP); 
  myservo1.attach(servo1);  
  myservo2.attach(servo2);  
  Serial.begin(9600);
}



void loop(){
    digitalWrite(13, LOW);
    button=digitalRead(2);
    if(button==0){
      digitalWrite(13, HIGH);
      delay(50);
      }
    servoVal = analogRead(joyH);          
    servoVal = map(servoVal, 0, 1023, 0, 180);
    myservo2.write(servoVal);   
    delay(15);
    servoVal = analogRead(joyV);           
    servoVal = map(servoVal, 0, 1023, 0, 180);   
    myservo1.write(servoVal);                          
    delay(15);                         
}
