# Fritzing sketch LDLAnalogReadSerial2LCD_LED (saved by Fritzing 0.9.3b)
circuit board: 8.46667cm x 5.64444cm
breadboards: 1

parts:
  Onderdeel1 = Arduino Uno (Rev3)
  LCM1602_IIC1 = LCM1602 IIC [part_number="LCM1602 IIC" chip_label="LCM1602 IIC" package="DIP (Dual Inline) [THT]"]
  LCD1 = LCD screen  # not connected
  S1 = Momentary Switch [package=ksa_sealed_tac_switch]
  S2 = Momentary Switch [package=ksa_sealed_tac_switch]

nets:
  N1: Onderdeel1.A4/SDA, LCM1602_IIC1.SDA
  N2: Onderdeel1.A5/SCL, LCM1602_IIC1.SCL
  GND: Onderdeel1.GND, LCM1602_IIC1.GND, S1.4, S2.4
  N3: Onderdeel1.D2, S2.1
  N4: Onderdeel1.D3_PWM, S1.1
  5V: Onderdeel1.5V, LCM1602_IIC1.VCC
  N5: LCM1602_IIC1.LED_A, LCM1602_IIC1.LED_B

custom parts:
  LCM1602 IIC: I2C-Module to use a 1602 or 2004 LCD on with the wire.h libory Serial LCD Modul

// code stored in the sketch: AnalogReadSerial2LCD_LED.ino


#include <Wire.h>
#include <LiquidCrystal_I2C.h>
const int Gumb1 = 2;
const int Gumb2 = 3;
LiquidCrystal_I2C lcd(0x27, 16,2);
int broj = 0;


void setup() {
  // put your setup code here, to run once:
  lcd.init();
  lcd.backlight();
  pinMode(Gumb1, INPUT_PULLUP);
  pinMode(Gumb2, INPUT_PULLUP);
  lcd.setCursor(0, 1);
  lcd.print("test");
  delay (1500);
  lcd.clear();
}


void loop() {
  // put your main code here, to run repeatedly:


if (digitalRead(Gumb2)==LOW and digitalRead(Gumb1)==LOW) {
  lcd.clear();
  lcd.print("Reset");
  delay(300);
  broj = 0;
  lcd.clear();
  lcd.print(broj);
}
else if (digitalRead(Gumb1)==LOW) {
  lcd.clear();
  broj= broj + 1;
  lcd.print(broj);
  delay(125);
}
else if (digitalRead(Gumb2)==LOW) {
  lcd.clear();
  broj= broj - 1;
  lcd.print(broj);
  delay(125);
}



}
